// Logisim project MasterChef.circ as structural Verilog: 2 circuits, main circuit main
module main (
  input  Pause_Button,
  input  in_2,
  input  in_3,
  input  in_4,
  input  in_5,
  input  in_6,
  input  in_7,
  input  in_8,
  input  in_9,
  input  [1:0] in_10,
  input  in_11,
  input  in_12,
  input  in_13,
  input  in_14,
  input  in_15,
  input  in_16,
  input  in_17,
  input  in_18,
  input  [1:0] in_19,
  output out_20,
  output out_21,
  output out_22,
  output out_23,
  output out_24,
  output out_25
);

  wire and_1_out, and_2_out, and_3_out, and_4_out, and_5_out, and_6_out, and_7_out, and_8_out, and_9_out,
       and_10_out, and_11_out, and_12_out, and_13_out, and_14_out, and_15_out, and_16_out, and_17_out,
       and_18_out, and_19_out, and_20_out, and_21_out, and_22_out, and_23_out, and_24_out, and_25_out,
       button_1_out, button_2_out, button_3_out, button_4_out, button_5_out, button_6_out, clock_1_out,
       d_ff_1_q, d_ff_2_q, d_ff_3_q, d_ff_4_q, d_ff_5_q, d_ff_6_q, d_ff_7_q, d_ff_8_q, d_ff_9_q, d_ff_10_q,
       d_ff_11_q, d_ff_12_q, d_ff_13_q, d_ff_14_q, d_ff_15_q, d_ff_16_q, j_k_ff_1_qn, j_k_ff_2_qn,
       j_k_ff_3_q, j_k_ff_4_qn, j_k_ff_5_q, j_k_ff_6_q, j_k_ff_6_qn, j_k_ff_7_q, j_k_ff_7_qn, j_k_ff_9_q,
       j_k_ff_9_qn, j_k_ff_10_q, j_k_ff_10_qn, j_k_ff_11_q, j_k_ff_11_qn, j_k_ff_12_qn, j_k_ff_13_q,
       j_k_ff_13_qn, j_k_ff_15_qn, j_k_ff_16_q, j_k_ff_17_q, j_k_ff_18_q, j_k_ff_19_q, j_k_ff_20_q,
       j_k_ff_20_qn, j_k_ff_21_q, j_k_ff_21_qn, j_k_ff_22_q, j_k_ff_22_qn, j_k_ff_23_q, j_k_ff_23_qn,
       j_k_ff_24_q, j_k_ff_24_qn, j_k_ff_25_q, j_k_ff_25_qn, j_k_ff_26_q, j_k_ff_26_qn, j_k_ff_27_q,
       j_k_ff_27_qn, j_k_ff_28_q, j_k_ff_28_qn, j_k_ff_29_q, j_k_ff_30_q, j_k_ff_31_q, j_k_ff_32_q,
       j_k_ff_33_q, j_k_ff_34_q, j_k_ff_35_q, j_k_ff_36_q, j_k_ff_37_q, j_k_ff_38_q, multiplexer_1_out,
       multiplexer_2_out, multiplexer_3_out, multiplexer_4_out, multiplexer_5_out, multiplexer_6_out,
       multiplexer_7_out, multiplexer_8_out, multiplexer_9_out, n4to7_1_a_2, n4to7_1_b_2, n4to7_1_c_2,
       n4to7_1_d_2, n4to7_1_e, n4to7_1_f, n4to7_1_g, n4to7_2_a_2, n4to7_2_b_2, n4to7_2_c_2, n4to7_2_d_2,
       n4to7_2_e, n4to7_2_f, n4to7_2_g, n4to7_3_a_2, n4to7_3_b_2, n4to7_3_c_2, n4to7_3_d_2, n4to7_3_e,
       n4to7_3_f, n4to7_3_g, n4to7_4_a_2, n4to7_4_b_2, n4to7_4_c_2, n4to7_4_d_2, n4to7_4_e, n4to7_4_f,
       n4to7_4_g, n4to7_5_a_2, n4to7_5_b_2, n4to7_5_c_2, n4to7_5_d_2, n4to7_5_e, n4to7_5_f, n4to7_5_g,
       n4to7_6_a_2, n4to7_6_b_2, n4to7_6_c_2, n4to7_6_d_2, n4to7_6_e, n4to7_6_f, n4to7_6_g, not_1_out,
       or_1_out, or_2_out, or_3_out, or_4_out, or_5_out, or_6_out, or_7_out, or_8_out, or_9_out, or_10_out,
       or_11_out, or_12_out, or_13_out, or_14_out, or_15_out, xnor_1_out, xnor_2_out, xnor_3_out, xnor_4_out,
       xnor_5_out, xnor_6_out, xnor_7_out, xnor_8_out, xnor_9_out, xnor_10_out, xnor_11_out, xnor_12_out,
       xnor_13_out, xnor_14_out, xnor_15_out, xnor_16_out;

  buf or_1 (or_1_out, or_12_out);  // OR_Gate
  J_K_Flip_Flop j_k_ff_1 (
    .J(1'b1), .clk(or_1_out), .K(1'b1), .Q(out_25), .Qn(j_k_ff_1_qn), .reset(or_2_out));  // open: preset, en
  J_K_Flip_Flop j_k_ff_2 (
    .J(1'b1), .clk(j_k_ff_1_qn), .K(1'b1), .Q(out_24), .Qn(j_k_ff_2_qn), .reset(or_2_out));  // open: preset, en
  or or_2 (or_2_out, and_2_out, button_3_out);
  and and_1 (and_1_out, out_25, out_24);
  and and_2 (and_2_out, and_1_out, out_23);
  J_K_Flip_Flop j_k_ff_3 (
    .J(1'b1), .clk(j_k_ff_6_qn), .K(1'b1), .Q(j_k_ff_3_q), .reset(or_3_out));  // open: Qn, preset, en
  J_K_Flip_Flop j_k_ff_4 (
    .J(1'b1), .clk(j_k_ff_2_qn), .K(1'b1), .Q(out_23), .Qn(j_k_ff_4_qn), .reset(or_2_out));  // open: preset, en
  or or_3 (or_3_out, out_21, and_7_out, and_14_out, and_3_out, button_3_out, and_8_out);
  J_K_Flip_Flop j_k_ff_5 (
    .J(1'b1), .clk(j_k_ff_7_qn), .K(1'b1), .Q(j_k_ff_5_q), .reset(or_4_out));  // open: Qn, preset, en
  J_K_Flip_Flop j_k_ff_6 (
    .J(1'b1), .clk(j_k_ff_9_qn), .K(1'b1), .Q(j_k_ff_6_q), .Qn(j_k_ff_6_qn), .reset(or_3_out));  // open: preset, en
  Button button_1 (.out(button_1_out));
  J_K_Flip_Flop j_k_ff_7 (
    .J(1'b1), .clk(j_k_ff_10_qn), .K(1'b1), .Q(j_k_ff_7_q), .Qn(j_k_ff_7_qn), .reset(or_4_out));  // open: preset, en
  Button button_2 (.out(button_2_out));
  and and_3 (and_3_out, j_k_ff_3_q, j_k_ff_9_q);
  and and_4 (and_4_out, button_1_out, and_11_out);
  or or_4 (or_4_out, j_k_ff_16_q, button_3_out, and_19_out, and_5_out, and_6_out, and_9_out);
  and and_5 (and_5_out, j_k_ff_5_q, j_k_ff_10_q);
  and and_6 (and_6_out, and_12_out, j_k_ff_30_q);
  J_K_Flip_Flop j_k_ff_8 (.J(1'b1), .clk(j_k_ff_4_qn), .K(1'b1), .Q(out_22), .reset(or_2_out));  // open: Qn, preset, en
  J_K_Flip_Flop j_k_ff_9 (
    .J(1'b1), .clk(j_k_ff_11_qn), .K(1'b1), .Q(j_k_ff_9_q), .Qn(j_k_ff_9_qn), .reset(or_3_out));  // open: preset, en
  or or_5 (or_5_out, button_1_out, and_17_out);
  and and_7 (and_7_out, Pause_Button, and_14_out);
  and and_8 (and_8_out, and_11_out, j_k_ff_29_q);
  J_K_Flip_Flop j_k_ff_10 (
    .J(1'b1), .clk(j_k_ff_13_qn), .K(1'b1), .Q(j_k_ff_10_q), .Qn(j_k_ff_10_qn), .reset(or_4_out));  // open: preset, en
  or or_6 (or_6_out, button_2_out, and_18_out);
  J_K_Flip_Flop j_k_ff_11 (
    .J(1'b1), .clk(or_5_out), .K(1'b1), .Q(j_k_ff_11_q), .Qn(j_k_ff_11_qn), .reset(or_3_out));  // open: preset, en
  D_Flip_Flop d_ff_1 (.clk(button_3_out), .D(in_2), .Q(d_ff_1_q));  // open: Qn, preset, en, reset
  J_K_Flip_Flop j_k_ff_12 (
    .J(1'b1), .clk(and_4_out), .K(1'b1), .Q(out_20), .Qn(j_k_ff_12_qn), .reset(or_3_out));  // open: preset, en
  J_K_Flip_Flop j_k_ff_13 (
    .J(1'b1), .clk(or_6_out), .K(1'b1), .Q(j_k_ff_13_q), .Qn(j_k_ff_13_qn), .reset(or_4_out));  // open: preset, en
  D_Flip_Flop d_ff_2 (.clk(button_3_out), .D(in_11), .Q(d_ff_2_q));  // open: Qn, preset, en, reset
  and and_9 (and_9_out, Pause_Button, and_19_out);
  xnor xnor_1 (xnor_1_out, d_ff_1_q, j_k_ff_3_q);
  xnor xnor_2 (xnor_2_out, d_ff_2_q, j_k_ff_5_q);
  and and_10 (and_10_out, and_12_out, button_2_out);
  D_Flip_Flop d_ff_3 (.clk(button_3_out), .D(in_3), .Q(d_ff_3_q));  // open: Qn, preset, en, reset
  xnor xnor_3 (xnor_3_out, d_ff_3_q, j_k_ff_6_q);
  J_K_Flip_Flop j_k_ff_14 (
    .J(1'b1), .clk(j_k_ff_12_qn), .K(1'b1), .Q(out_21), .reset(or_3_out));  // open: Qn, preset, en
  D_Flip_Flop d_ff_4 (.clk(button_3_out), .D(in_12), .Q(d_ff_4_q));  // open: Qn, preset, en, reset
  xnor xnor_4 (xnor_4_out, d_ff_4_q, j_k_ff_7_q);
  D_Flip_Flop d_ff_5 (.clk(button_3_out), .D(in_4), .Q(d_ff_5_q));  // open: Qn, preset, en, reset
  and and_11 (and_11_out, xnor_1_out, xnor_3_out, xnor_5_out, xnor_7_out);
  D_Flip_Flop d_ff_6 (.clk(button_3_out), .D(in_13), .Q(d_ff_6_q));  // open: Qn, preset, en, reset
  and and_12 (and_12_out, xnor_2_out, xnor_4_out, xnor_6_out, xnor_8_out);
  J_K_Flip_Flop j_k_ff_15 (.J(1'b1), .clk(and_10_out), .K(1'b1), .Qn(j_k_ff_15_qn));  // open: Q, preset, en, reset
  xnor xnor_5 (xnor_5_out, d_ff_5_q, j_k_ff_9_q);
  xnor xnor_6 (xnor_6_out, d_ff_6_q, j_k_ff_10_q);
  J_K_Flip_Flop j_k_ff_16 (.J(1'b1), .clk(j_k_ff_15_qn), .K(1'b1), .Q(j_k_ff_16_q));  // open: Qn, preset, en, reset
  D_Flip_Flop d_ff_7 (.clk(button_3_out), .D(in_5), .Q(d_ff_7_q));  // open: Qn, preset, en, reset
  xnor xnor_7 (xnor_7_out, d_ff_7_q, j_k_ff_11_q);
  D_Flip_Flop d_ff_8 (.clk(button_3_out), .D(in_14), .Q(d_ff_8_q));  // open: Qn, preset, en, reset
  xnor xnor_8 (xnor_8_out, d_ff_8_q, j_k_ff_13_q);
  Multiplexer #(.select(2), .enable("false")) multiplexer_1 (
    .in0(1'b0), .in1(1'b0), .in2(j_k_ff_38_q), .out(multiplexer_1_out), .sel(in_19));  // open: in3
  Multiplexer #(.select(2), .enable("false")) multiplexer_2 (
    .in0(1'b0), .in1(1'b0), .in2(j_k_ff_36_q), .out(multiplexer_2_out), .sel(in_19));  // open: in3
  Multiplexer #(.select(2), .enable("false")) multiplexer_3 (
    .in0(1'b0), .in1(1'b0), .in2(j_k_ff_34_q), .out(multiplexer_3_out), .sel(in_19));  // open: in3
  Multiplexer #(.select(2), .enable("false")) multiplexer_4 (
    .in0(1'b0), .in1(1'b0), .in2(j_k_ff_32_q), .out(multiplexer_4_out), .sel(in_19));  // open: in3
  _4to7 u_4to7_1 (
    .D(j_k_ff_3_q), .C(j_k_ff_6_q), .B(j_k_ff_9_q), .A(j_k_ff_11_q), .a_2(n4to7_1_a_2), .b_2(n4to7_1_b_2),
    .c_2(n4to7_1_c_2), .d_2(n4to7_1_d_2), .e(n4to7_1_e), .f(n4to7_1_f), .g(n4to7_1_g));
  _4to7 u_4to7_2 (
    .D(j_k_ff_5_q), .C(j_k_ff_7_q), .B(j_k_ff_10_q), .A(j_k_ff_13_q), .a_2(n4to7_2_a_2), .b_2(n4to7_2_b_2),
    .c_2(n4to7_2_c_2), .d_2(n4to7_2_d_2), .e(n4to7_2_e), .f(n4to7_2_f), .g(n4to7_2_g));
  _4to7 u_4to7_3 (
    .D(multiplexer_1_out), .C(multiplexer_2_out), .B(multiplexer_3_out), .A(multiplexer_4_out),
    .a_2(n4to7_3_a_2), .b_2(n4to7_3_b_2), .c_2(n4to7_3_c_2), .d_2(n4to7_3_d_2), .e(n4to7_3_e), .f(n4to7_3_f),
    .g(n4to7_3_g));
  _7_Segment_Display u_7_segment_display_1 (
    .g(n4to7_1_g), .f(n4to7_1_f), .a(n4to7_1_a_2), .b(n4to7_1_b_2), .e(n4to7_1_e), .d(n4to7_1_d_2),
    .c(n4to7_1_c_2));  // open: dp
  _7_Segment_Display u_7_segment_display_2 (
    .g(n4to7_2_g), .f(n4to7_2_f), .a(n4to7_2_a_2), .b(n4to7_2_b_2), .e(n4to7_2_e), .d(n4to7_2_d_2),
    .c(n4to7_2_c_2));  // open: dp
  _7_Segment_Display u_7_segment_display_3 (
    .g(n4to7_3_g), .f(n4to7_3_f), .a(n4to7_3_a_2), .b(n4to7_3_b_2), .e(n4to7_3_e), .d(n4to7_3_d_2),
    .c(n4to7_3_c_2));  // open: dp
  and and_13 (and_13_out, Pause_Button, and_11_out, and_21_out);
  Button button_3 (.out(button_3_out));
  J_K_Flip_Flop j_k_ff_17 (
    .J(1'b1), .clk(j_k_ff_20_qn), .K(1'b1), .Q(j_k_ff_17_q), .reset(or_7_out));  // open: Qn, preset, en
  J_K_Flip_Flop j_k_ff_18 (
    .J(1'b1), .clk(j_k_ff_21_qn), .K(1'b1), .Q(j_k_ff_18_q), .reset(or_8_out));  // open: Qn, preset, en
  J_K_Flip_Flop j_k_ff_19 (
    .J(1'b1), .clk(j_k_ff_22_qn), .K(1'b1), .Q(j_k_ff_19_q), .reset(or_9_out));  // open: Qn, preset, en
  not not_1 (not_1_out, Pause_Button);
  J_K_Flip_Flop j_k_ff_20 (
    .J(1'b1), .clk(j_k_ff_23_qn), .K(1'b1), .Q(j_k_ff_20_q), .Qn(j_k_ff_20_qn), .reset(or_7_out));  // open: preset, en
  and and_14 (and_14_out, and_11_out, and_21_out);
  J_K_Flip_Flop j_k_ff_21 (
    .J(1'b1), .clk(j_k_ff_24_qn), .K(1'b1), .Q(j_k_ff_21_q), .Qn(j_k_ff_21_qn), .reset(or_8_out));  // open: preset, en
  and and_15 (and_15_out, Pause_Button, and_12_out, and_22_out);
  and and_16 (and_16_out, not_1_out, clock_1_out);
  Clock clock_1 (.out(clock_1_out));
  Button button_4 (.out(button_4_out));
  or or_7 (or_7_out, and_13_out, and_14_out, and_17_out, button_3_out);
  and and_17 (and_17_out, j_k_ff_17_q, j_k_ff_23_q);
  Button button_5 (.out(button_5_out));
  or or_8 (or_8_out, button_3_out, and_19_out, and_18_out, and_15_out);
  and and_18 (and_18_out, j_k_ff_18_q, j_k_ff_24_q);
  and and_19 (and_19_out, and_12_out, and_22_out);
  J_K_Flip_Flop j_k_ff_22 (
    .J(1'b1), .clk(j_k_ff_25_qn), .K(1'b1), .Q(j_k_ff_22_q), .Qn(j_k_ff_22_qn), .reset(or_9_out));  // open: preset, en
  or or_9 (or_9_out, button_3_out, and_20_out);
  and and_20 (and_20_out, j_k_ff_19_q, j_k_ff_25_q);
  or or_10 (or_10_out, and_16_out, button_4_out);
  J_K_Flip_Flop j_k_ff_23 (
    .J(1'b1), .clk(j_k_ff_26_qn), .K(1'b1), .Q(j_k_ff_23_q), .Qn(j_k_ff_23_qn), .reset(or_7_out));  // open: preset, en
  or or_11 (or_11_out, and_14_out, button_5_out);
  J_K_Flip_Flop j_k_ff_24 (
    .J(1'b1), .clk(j_k_ff_27_qn), .K(1'b1), .Q(j_k_ff_24_q), .Qn(j_k_ff_24_qn), .reset(or_8_out));  // open: preset, en
  Button button_6 (.out(button_6_out));
  J_K_Flip_Flop j_k_ff_25 (
    .J(1'b1), .clk(j_k_ff_28_qn), .K(1'b1), .Q(j_k_ff_25_q), .Qn(j_k_ff_25_qn), .reset(or_9_out));  // open: preset, en
  J_K_Flip_Flop j_k_ff_26 (
    .J(1'b1), .clk(or_10_out), .K(1'b1), .Q(j_k_ff_26_q), .Qn(j_k_ff_26_qn), .reset(or_7_out));  // open: preset, en
  D_Flip_Flop d_ff_9 (.clk(button_3_out), .D(in_6), .Q(d_ff_9_q));  // open: Qn, preset, en, reset
  or or_12 (or_12_out, and_19_out, button_6_out);
  xnor xnor_9 (xnor_9_out, d_ff_9_q, j_k_ff_17_q);
  J_K_Flip_Flop j_k_ff_27 (
    .J(1'b1), .clk(or_11_out), .K(1'b1), .Q(j_k_ff_27_q), .Qn(j_k_ff_27_qn), .reset(or_8_out));  // open: preset, en
  D_Flip_Flop d_ff_10 (.clk(button_3_out), .D(in_15), .Q(d_ff_10_q));  // open: Qn, preset, en, reset
  xnor xnor_10 (xnor_10_out, d_ff_10_q, j_k_ff_18_q);
  J_K_Flip_Flop j_k_ff_28 (
    .J(1'b1), .clk(or_12_out), .K(1'b1), .Q(j_k_ff_28_q), .Qn(j_k_ff_28_qn), .reset(or_9_out));  // open: preset, en
  D_Flip_Flop d_ff_11 (.clk(button_3_out), .D(in_7), .Q(d_ff_11_q));  // open: Qn, preset, en, reset
  xnor xnor_11 (xnor_11_out, d_ff_11_q, j_k_ff_20_q);
  J_K_Flip_Flop j_k_ff_29 (
    .J(1'b1), .K(1'b1), .Q(j_k_ff_29_q), .preset(and_21_out), .reset(or_7_out));  // open: clk, Qn, en
  D_Flip_Flop d_ff_12 (.clk(button_3_out), .D(in_16), .Q(d_ff_12_q));  // open: Qn, preset, en, reset
  xnor xnor_12 (xnor_12_out, d_ff_12_q, j_k_ff_21_q);
  D_Flip_Flop d_ff_13 (.clk(button_3_out), .D(in_8), .Q(d_ff_13_q));  // open: Qn, preset, en, reset
  and and_21 (and_21_out, xnor_9_out, xnor_11_out, xnor_13_out, xnor_15_out);
  and and_22 (and_22_out, xnor_10_out, xnor_12_out, xnor_14_out, xnor_16_out);
  J_K_Flip_Flop j_k_ff_30 (
    .J(1'b1), .K(1'b1), .Q(j_k_ff_30_q), .preset(and_22_out), .reset(or_8_out));  // open: clk, Qn, en
  xnor xnor_13 (xnor_13_out, d_ff_13_q, j_k_ff_23_q);
  D_Flip_Flop d_ff_14 (.clk(button_3_out), .D(in_17), .Q(d_ff_14_q));  // open: Qn, preset, en, reset
  xnor xnor_14 (xnor_14_out, d_ff_14_q, j_k_ff_24_q);
  D_Flip_Flop d_ff_15 (.clk(button_3_out), .D(in_9), .Q(d_ff_15_q));  // open: Qn, preset, en, reset
  xnor xnor_15 (xnor_15_out, d_ff_15_q, j_k_ff_26_q);
  D_Flip_Flop d_ff_16 (.clk(button_3_out), .D(in_18), .Q(d_ff_16_q));  // open: Qn, preset, en, reset
  xnor xnor_16 (xnor_16_out, d_ff_16_q, j_k_ff_27_q);
  Multiplexer #(.select(2), .enable("false")) multiplexer_5 (
    .in0(out_23), .in1(j_k_ff_22_q), .in2(j_k_ff_35_q), .out(multiplexer_5_out), .sel(in_19));  // open: in3
  Multiplexer #(.select(2), .enable("false")) multiplexer_6 (
    .in0(out_24), .in1(j_k_ff_25_q), .in2(j_k_ff_33_q), .out(multiplexer_6_out), .sel(in_19));  // open: in3
  Multiplexer #(.select(2), .enable("false")) multiplexer_7 (
    .in0(out_25), .in1(j_k_ff_28_q), .in2(j_k_ff_31_q), .out(multiplexer_7_out), .sel(in_19));  // open: in3
  _4to7 u_4to7_4 (
    .D(j_k_ff_17_q), .C(j_k_ff_20_q), .B(j_k_ff_23_q), .A(j_k_ff_26_q), .a_2(n4to7_4_a_2), .b_2(n4to7_4_b_2),
    .c_2(n4to7_4_c_2), .d_2(n4to7_4_d_2), .e(n4to7_4_e), .f(n4to7_4_f), .g(n4to7_4_g));
  _4to7 u_4to7_5 (
    .D(j_k_ff_18_q), .C(j_k_ff_21_q), .B(j_k_ff_24_q), .A(j_k_ff_27_q), .a_2(n4to7_5_a_2), .b_2(n4to7_5_b_2),
    .c_2(n4to7_5_c_2), .d_2(n4to7_5_d_2), .e(n4to7_5_e), .f(n4to7_5_f), .g(n4to7_5_g));
  or or_13 (or_13_out, button_3_out, or_14_out);
  Multiplexer #(.select(2), .enable("false")) multiplexer_8 (
    .in0(out_22), .in1(j_k_ff_19_q), .in2(j_k_ff_37_q), .out(multiplexer_8_out), .sel(in_19));  // open: in3
  _7_Segment_Display u_7_segment_display_4 (
    .g(n4to7_4_g), .f(n4to7_4_f), .a(n4to7_4_a_2), .b(n4to7_4_b_2), .e(n4to7_4_e), .d(n4to7_4_d_2),
    .c(n4to7_4_c_2));  // open: dp
  _7_Segment_Display u_7_segment_display_5 (
    .g(n4to7_5_g), .f(n4to7_5_f), .a(n4to7_5_a_2), .b(n4to7_5_b_2), .e(n4to7_5_e), .d(n4to7_5_d_2),
    .c(n4to7_5_c_2));  // open: dp
  J_K_Flip_Flop #(.trigger("falling")) j_k_ff_31 (
    .J(1'b1), .clk(or_12_out), .K(1'b1), .Q(j_k_ff_31_q), .reset(or_13_out));  // open: Qn, preset, en
  J_K_Flip_Flop #(.trigger("falling")) j_k_ff_32 (
    .J(1'b1), .clk(and_23_out), .K(1'b1), .Q(j_k_ff_32_q), .reset(or_15_out));  // open: Qn, preset, en
  _7_Segment_Display u_7_segment_display_6 (
    .g(n4to7_6_g), .f(n4to7_6_f), .a(n4to7_6_a_2), .b(n4to7_6_b_2), .e(n4to7_6_e), .d(n4to7_6_d_2),
    .c(n4to7_6_c_2));  // open: dp
  _4to7 u_4to7_6 (
    .D(multiplexer_8_out), .C(multiplexer_5_out), .B(multiplexer_6_out), .A(multiplexer_7_out),
    .a_2(n4to7_6_a_2), .b_2(n4to7_6_b_2), .c_2(n4to7_6_c_2), .d_2(n4to7_6_d_2), .e(n4to7_6_e), .f(n4to7_6_f),
    .g(n4to7_6_g));
  J_K_Flip_Flop #(.trigger("falling")) j_k_ff_33 (
    .J(1'b1), .clk(j_k_ff_31_q), .K(1'b1), .Q(j_k_ff_33_q), .reset(or_13_out));  // open: Qn, preset, en
  J_K_Flip_Flop #(.trigger("falling")) j_k_ff_34 (
    .J(1'b1), .clk(j_k_ff_32_q), .K(1'b1), .Q(j_k_ff_34_q), .reset(or_15_out));  // open: Qn, preset, en
  J_K_Flip_Flop #(.trigger("falling")) j_k_ff_35 (
    .J(1'b1), .clk(j_k_ff_33_q), .K(1'b1), .Q(j_k_ff_35_q), .reset(or_13_out));  // open: Qn, preset, en
  J_K_Flip_Flop #(.trigger("falling")) j_k_ff_36 (
    .J(1'b1), .clk(j_k_ff_34_q), .K(1'b1), .Q(j_k_ff_36_q), .reset(or_15_out));  // open: Qn, preset, en
  J_K_Flip_Flop #(.trigger("falling")) j_k_ff_37 (
    .J(1'b1), .clk(j_k_ff_35_q), .K(1'b1), .Q(j_k_ff_37_q), .reset(or_13_out));  // open: Qn, preset, en
  J_K_Flip_Flop #(.trigger("falling")) j_k_ff_38 (
    .J(1'b1), .clk(j_k_ff_36_q), .K(1'b1), .Q(j_k_ff_38_q), .reset(or_15_out));  // open: Qn, preset, en
  Multiplexer #(.select(2), .enable("false")) multiplexer_9 (
    .in0(or_10_out), .in1(or_11_out), .in2(or_12_out), .out(multiplexer_9_out), .sel(in_10));  // open: in3
  and and_23 (and_23_out, j_k_ff_33_q, j_k_ff_37_q);
  or or_14 (or_14_out, and_23_out, and_25_out);
  or or_15 (or_15_out, and_25_out, button_3_out);
  LED led_1 (.in(multiplexer_9_out));
  and and_24 (and_24_out, j_k_ff_35_q, j_k_ff_31_q);
  and and_25 (and_25_out, j_k_ff_32_q, and_24_out);

  // Notes on the sheet:
  //   Second 2 Pulse 
  //   Minute 2 Pulse
  //   Reset Button
  //   Second Pulse
  //   Minute Pulse
  //   Hour Pulse
  //   44
  //   Signal for the first flip flop of hour will go from here
endmodule

module _4to7 (
  input  D,
  input  C,
  input  B,
  input  A,
  output a_2,
  output b_2,
  output c_2,
  output d_2,
  output e,
  output f,
  output g
);

  wire and_1_out, and_2_out, and_3_out, and_4_out, and_5_out, and_6_out, and_7_out, and_8_out, and_9_out,
       and_10_out, and_11_out, and_12_out, and_13_out, and_14_out, and_15_out, and_16_out, not_1_out,
       not_2_out, not_3_out, not_4_out, not_5_out, not_6_out, not_7_out, not_8_out, not_9_out, not_10_out,
       not_11_out, not_12_out, not_13_out, not_14_out, not_15_out, not_16_out, not_17_out, not_18_out,
       not_19_out, not_20_out, not_21_out;

  not not_1 (not_1_out, C);
  and and_1 (and_1_out, not_1_out, not_2_out);
  not not_2 (not_2_out, A);
  and and_2 (and_2_out, C, A);
  not not_3 (not_3_out, C);
  not not_4 (not_4_out, B);
  and and_3 (and_3_out, not_4_out, not_5_out);
  not not_5 (not_5_out, A);
  and and_4 (and_4_out, B, A);
  not not_6 (not_6_out, B);
  or or_1 (c_2, not_6_out, A, C);
  not not_7 (not_7_out, C);
  and and_5 (and_5_out, not_7_out, not_8_out);
  not not_8 (not_8_out, A);
  not not_9 (not_9_out, C);
  and and_6 (and_6_out, not_9_out, B);
  and and_7 (and_7_out, B, not_10_out);
  not not_10 (not_10_out, A);
  not not_11 (not_11_out, B);
  and and_8 (and_8_out, C, not_11_out, A);
  not not_12 (not_12_out, C);
  and and_9 (and_9_out, not_12_out, not_13_out);
  not not_13 (not_13_out, A);
  and and_10 (and_10_out, B, not_14_out);
  not not_14 (not_14_out, A);
  not not_15 (not_15_out, B);
  and and_11 (and_11_out, not_15_out, not_16_out);
  not not_16 (not_16_out, A);
  and and_12 (and_12_out, C, not_17_out);
  not not_17 (not_17_out, B);
  and and_13 (and_13_out, C, not_18_out);
  not not_18 (not_18_out, A);
  not not_19 (not_19_out, C);
  and and_14 (and_14_out, not_19_out, B);
  and and_15 (and_15_out, C, not_20_out);
  not not_20 (not_20_out, B);
  and and_16 (and_16_out, C, not_21_out);
  not not_21 (not_21_out, A);
  or or_2 (a_2, and_1_out, B, and_2_out, D);
  or or_3 (b_2, not_3_out, and_3_out, and_4_out);
  or or_4 (d_2, and_5_out, and_6_out, and_7_out, and_8_out, D);
  or or_5 (e, and_9_out, and_10_out);
  or or_6 (f, and_11_out, and_12_out, and_13_out, D);
  or or_7 (g, and_14_out, and_15_out, and_16_out, D);
endmodule
